# Fritzing sketch tvbacklightesp8266_v1.3 (saved by Fritzing 0.9.3b)
circuit board: 10.6321cm x 7.47319cm
breadboards: 1

parts:
  C0_1kµF = Electrolytic Capacitor [capacitance=1000µF package="300 mil [THT, electrolytic]"]
  GNDIn = Header 1 [package=smtso-256-et]
  DOut = Header 1 [package=smtso-256-et]
  VIn = Header 1 [package=smtso-256-et]
  GNDIn_2 = Header 1 [package=smtso-256-et]
  VOut = Header 1 [package=smtso-256-et]
  GNDOut = Header 1 [package=smtso-256-et]
  Vout = Header 1 [package=smtso-256-et]
  GNDIn_3 = Header 1 [package=smtso-256-et]
  VIn_2 = Header 1 [package=smtso-256-et]
  GNDOut_2 = Header 1 [package=smtso-256-et]
  Vin = Header 1 [package=smtso-256-et]
  VOut_2 = Header 1 [package=smtso-256-et]
  GNDOut_3 = Header 1 [package=smtso-256-et]
  C2_1kµF = Electrolytic Capacitor [capacitance=1000µF package="300 mil [THT, electrolytic]"]
  C3_1kµF = Electrolytic Capacitor [capacitance=1000µF package="300 mil [THT, electrolytic]"]
  ESP8266 = NodeMCU V3.0
  R470 = Resistor [tolerance=±5% resistance=470 power=5 package=THT]
  C1_1kµF1 = Electrolytic Capacitor [capacitance=1000µF package="300 mil [THT, electrolytic]"]
  GNDIn1 = Header 1 [package=smtso-256-et]
  GNDOut_4 = Header 1 [package=smtso-256-et]
  VOut1 = Header 1 [package=smtso-256-et]
  VIn1 = Header 1 [package=smtso-256-et]
  U1 = SWITCH_SPDT [package=kps-1290]
  bypass_C2 = Solder Jumper [package=sj_2s-no]
  bypass_C1 = Solder Jumper [package=sj_2s-no]
  bypass_C3 = Solder Jumper [package=sj_2s-no]

nets:
  N1: C0_1kµF.-, GNDIn.1, GNDIn_2.1, GNDOut.1, GNDIn_3.1, GNDOut_2.1, GNDOut_3.1, C2_1kµF.-, C3_1kµF.-, ESP8266.GND#6, ESP8266.GND#13, ESP8266.GND#16, ESP8266.GND#33, C1_1kµF1.-, GNDIn1.1, GNDOut_4.1
  N2: C0_1kµF.+, VIn.1, VOut_2.1, U1.O, bypass_C1.1
  N3: DOut.1, R470.Pin_0
  N4: VOut.1, VIn_2.1, C2_1kµF.+, bypass_C2.2, bypass_C3.2
  N5: Vout.1, Vin.1, C3_1kµF.+, bypass_C3.1
  N6: ESP8266.D4, R470.Pin_1
  N7: ESP8266.A0, U1.P
  N8: C1_1kµF1.+, VOut1.1, VIn1.1, bypass_C2.1, bypass_C1.2

notes:
  OFF
  Data

custom parts:
  NodeMCU V3.0: ESP8266 based NodeMCU
