# Fritzing sketch tvbacklightnano (saved by Fritzing 0.9.3b)
circuit board: 6.16479cm x 6.71427cm
breadboards: 1

parts:
  C1_1kµF = Electrolytic Capacitor [capacitance=1000µF package="300 mil [THT, electrolytic]"]
  GNDIn = Header 1 [package=smtso-256-et]
  DOut = Header 1 [package=smtso-256-et]
  VIn = Header 1 [package=smtso-256-et]
  GNDIn_2 = Header 1 [package=smtso-256-et]
  VOut = Header 1 [package=smtso-256-et]
  GNDOut = Header 1 [package=smtso-256-et]
  Vout = Header 1 [package=smtso-256-et]
  GNDIn_3 = Header 1 [package=smtso-256-et]
  VIn_2 = Header 1 [package=smtso-256-et]
  GNDOut_2 = Header 1 [package=smtso-256-et]
  Vin = Header 1 [package=smtso-256-et]
  VOut_2 = Header 1 [package=smtso-256-et]
  GNDOut_3 = Header 1 [package=smtso-256-et]
  C2_1kµF = Electrolytic Capacitor [capacitance=1000µF package="300 mil [THT, electrolytic]"]
  C3_1kµF = Electrolytic Capacitor [capacitance=1000µF package="300 mil [THT, electrolytic]"]
  Arduino_Uno = Arduino Nano (Rev3.0)
  R470 = Resistor [tolerance=±5% resistance=470 package=THT]

nets:
  N1: C1_1kµF.-, GNDIn.1, GNDIn_2.1, GNDOut.1, GNDIn_3.1, GNDOut_2.1, GNDOut_3.1, C2_1kµF.-, C3_1kµF.-, Arduino_Uno.GND
  N2: C1_1kµF.+, VIn.1, VOut_2.1
  N3: DOut.1, R470.Pin_0
  N4: VOut.1, VIn_2.1, C2_1kµF.+
  N5: Vout.1, Vin.1, C3_1kµF.+
  N6: Arduino_Uno.D11/MOSI, R470.Pin_1
